// Logisim project TOY_8.circ as structural Verilog: 31 circuits, main circuit full_circuit
module full_circuit (
  input  A,
  input  B,
  input  CIN,
  output SUM,
  output COUT
);

  wire and_1_out, and_2_out, xor_1_out;

  xor xor_1 (xor_1_out, A, B);
  and and_1 (and_1_out, A, B);
  xor xor_2 (SUM, xor_1_out, CIN);
  and and_2 (and_2_out, xor_1_out, CIN);
  or or_1 (COUT, and_1_out, and_2_out);
  // Probe on {COUT, SUM}
endmodule

module ADDER_8_bit (
  input  [7:0] A,
  input  [7:0] B,
  input  CIN,
  output [7:0] out_4,
  output out_5
);

  wire full_circuit_1_cout, full_circuit_2_cout, full_circuit_3_cout, full_circuit_4_cout,
       full_circuit_5_cout, full_circuit_6_cout, full_circuit_7_cout;

  // Probe on B
  // Probe on A
  full_circuit full_circuit_1 (.A(A[0]), .B(B[0]), .CIN(CIN), .SUM(out_4[0]), .COUT(full_circuit_1_cout));
  full_circuit full_circuit_2 (
    .A(A[1]), .B(B[1]), .CIN(full_circuit_1_cout), .SUM(out_4[1]), .COUT(full_circuit_2_cout));
  full_circuit full_circuit_3 (
    .A(A[2]), .B(B[2]), .CIN(full_circuit_2_cout), .SUM(out_4[2]), .COUT(full_circuit_3_cout));
  full_circuit full_circuit_4 (
    .A(A[3]), .B(B[3]), .CIN(full_circuit_3_cout), .SUM(out_4[3]), .COUT(full_circuit_4_cout));
  full_circuit full_circuit_5 (
    .A(A[4]), .B(B[4]), .CIN(full_circuit_4_cout), .SUM(out_4[4]), .COUT(full_circuit_5_cout));
  full_circuit full_circuit_6 (
    .A(A[5]), .B(B[5]), .CIN(full_circuit_5_cout), .SUM(out_4[5]), .COUT(full_circuit_6_cout));
  full_circuit full_circuit_7 (
    .A(A[6]), .B(B[6]), .CIN(full_circuit_6_cout), .SUM(out_4[6]), .COUT(full_circuit_7_cout));
  full_circuit full_circuit_8 (.A(A[7]), .B(B[7]), .CIN(full_circuit_7_cout), .SUM(out_4[7]), .COUT(out_5));
  // Probe on {out_5, out_4}
endmodule

module MUX (
  input  [3:0] in_1,
  input  [3:0] in_2,
  input  [3:0] in_3,
  input  [3:0] in_4,
  input  in_5,
  input  in_6,
  output [3:0] out_7
);

  wire and_1_out, and_2_out, and_3_out, nor_1_out, not_1_out, not_2_out;
  wire [3:0] controlled_buffer_1_out, controlled_buffer_2_out, controlled_buffer_3_out,
       controlled_buffer_4_out;

  assign controlled_buffer_1_out = nor_1_out ? in_1 : 4'bz;  // Controlled_Buffer controlled_buffer_1
  assign controlled_buffer_2_out = and_2_out ? in_2 : 4'bz;  // Controlled_Buffer controlled_buffer_2
  assign controlled_buffer_3_out = and_3_out ? in_3 : 4'bz;  // Controlled_Buffer controlled_buffer_3
  assign controlled_buffer_4_out = and_1_out ? in_4 : 4'bz;  // Controlled_Buffer controlled_buffer_4
  and and_1 (and_1_out, in_5, in_6);
  nor nor_1 (nor_1_out, in_5, in_6);
  not not_1 (not_1_out, in_5);
  Pull_Resistor pull_resistor_1 (.node(controlled_buffer_3_out));
  Pull_Resistor pull_resistor_2 (.node(controlled_buffer_4_out));
  and and_2 (and_2_out, not_1_out, in_6);
  Pull_Resistor pull_resistor_3 (.node(controlled_buffer_1_out));
  Pull_Resistor pull_resistor_4 (.node(controlled_buffer_2_out));
  and and_3 (and_3_out, not_2_out, in_5);
  not not_2 (not_2_out, in_6);
  assign out_7 = controlled_buffer_1_out | controlled_buffer_2_out | controlled_buffer_3_out | controlled_buffer_4_out;  // OR_Gate_part or_1, 4 bits wide
  // Probe on out_7
endmodule

module De_Coder (
  input  in_1,
  input  in_2,
  input  in_3,
  output _0,
  output _1,
  output _2,
  output _3,
  output _4,
  output _5,
  output _6,
  output _7
);

  wire not_1_out, not_2_out, not_3_out, not_4_out, not_5_out, not_6_out, not_7_out;

  // Probe on {in_1, in_2, in_3}
  not not_1 (not_1_out, in_2);
  not not_2 (not_2_out, in_1);
  not not_3 (not_3_out, in_3);
  not not_4 (not_4_out, in_1);
  not not_5 (not_5_out, in_1);
  not not_6 (not_6_out, in_3);
  not not_7 (not_7_out, in_2);
  and and_1 (_1, in_3, not_1_out, not_2_out);
  and and_2 (_2, not_3_out, in_2, not_4_out);
  and and_3 (_3, in_3, in_2, not_5_out);
  and and_4 (_4, not_6_out, not_7_out, in_1);
  and and_5 (_5, in_3, ~in_2, in_1);  // AND_Gate_part
  and and_6 (_6, ~in_3, in_2, in_1);  // AND_Gate_part
  and and_7 (_7, in_3, in_2, in_1);
  nor nor_1 (_0, in_3, in_2, in_1);
endmodule

module De_mux (
  input  in_1,
  input  in_2,
  input  in_3,
  input  [3:0] X,
  output [3:0] out_5,
  output [3:0] out_6,
  output [3:0] _2,
  output [3:0] _3,
  output [3:0] _4,
  output [3:0] _5,
  output [3:0] _6,
  output [3:0] _7
);

  wire and_1_out, and_2_out, and_3_out, and_4_out, and_5_out, and_6_out, and_7_out, nor_1_out, not_1_out,
       not_2_out, not_3_out, not_4_out, not_5_out, not_6_out, not_7_out;

  // Probe on {in_1, in_2, in_3}
  not not_1 (not_1_out, in_2);
  not not_2 (not_2_out, in_1);
  not not_3 (not_3_out, in_3);
  not not_4 (not_4_out, in_1);
  not not_5 (not_5_out, in_1);
  not not_6 (not_6_out, in_3);
  not not_7 (not_7_out, in_2);
  and and_1 (and_1_out, in_3, not_1_out, not_2_out);
  and and_2 (and_2_out, not_3_out, in_2, not_4_out);
  and and_3 (and_3_out, in_3, in_2, not_5_out);
  and and_4 (and_4_out, not_6_out, not_7_out, in_1);
  and and_5 (and_5_out, in_3, ~in_2, in_1);  // AND_Gate_part
  and and_6 (and_6_out, ~in_3, in_2, in_1);  // AND_Gate_part
  and and_7 (and_7_out, in_3, in_2, in_1);
  Pull_Resistor pull_resistor_1 (.node(out_5));
  assign out_5 = nor_1_out ? X : 4'bz;  // Controlled_Buffer controlled_buffer_1
  nor nor_1 (nor_1_out, in_3, in_2, in_1);
  Pull_Resistor pull_resistor_2 (.node(out_6));
  assign out_6 = and_1_out ? X : 4'bz;  // Controlled_Buffer controlled_buffer_2
  Pull_Resistor pull_resistor_3 (.node(_2));
  assign _2 = and_2_out ? X : 4'bz;  // Controlled_Buffer controlled_buffer_3
  Pull_Resistor pull_resistor_4 (.node(_3));
  assign _3 = and_3_out ? X : 4'bz;  // Controlled_Buffer controlled_buffer_4
  Pull_Resistor pull_resistor_5 (.node(_4));
  assign _4 = and_4_out ? X : 4'bz;  // Controlled_Buffer controlled_buffer_5
  Pull_Resistor pull_resistor_6 (.node(_5));
  assign _5 = and_5_out ? X : 4'bz;  // Controlled_Buffer controlled_buffer_6
  Pull_Resistor pull_resistor_7 (.node(_6));
  assign _6 = and_6_out ? X : 4'bz;  // Controlled_Buffer controlled_buffer_7
  Pull_Resistor pull_resistor_8 (.node(_7));
  assign _7 = and_7_out ? X : 4'bz;  // Controlled_Buffer controlled_buffer_8

  // Notes on the sheet:
  //   0
  //   1
endmodule

module De_coder_MUX (
  input  in_1,
  input  in_2,
  input  in_3,
  input  [3:0] X,
  output [3:0] out_5,
  output out_6,
  output [3:0] out_7,
  output out_8,
  output [3:0] _2,
  output out_10,
  output [3:0] _3,
  output out_12,
  output [3:0] _4,
  output out_14,
  output [3:0] _5,
  output out_16,
  output [3:0] _6,
  output out_18,
  output [3:0] _7,
  output out_20
);

  wire not_1_out, not_2_out, not_3_out, not_4_out, not_5_out, not_6_out, not_7_out;

  // Probe on {in_1, in_2, in_3}
  not not_1 (not_1_out, in_2);
  not not_2 (not_2_out, in_1);
  not not_3 (not_3_out, in_3);
  not not_4 (not_4_out, in_1);
  not not_5 (not_5_out, in_1);
  not not_6 (not_6_out, in_3);
  not not_7 (not_7_out, in_2);
  and and_1 (out_8, in_3, not_1_out, not_2_out);
  and and_2 (out_10, not_3_out, in_2, not_4_out);
  and and_3 (out_12, in_3, in_2, not_5_out);
  and and_4 (out_14, not_6_out, not_7_out, in_1);
  and and_5 (out_16, in_3, ~in_2, in_1);  // AND_Gate_part
  and and_6 (out_18, ~in_3, in_2, in_1);  // AND_Gate_part
  and and_7 (out_20, in_3, in_2, in_1);
  Pull_Resistor pull_resistor_1 (.node(out_5));
  assign out_5 = out_6 ? X : 4'bz;  // Controlled_Buffer controlled_buffer_1
  nor nor_1 (out_6, in_3, in_2, in_1);
  Pull_Resistor pull_resistor_2 (.node(out_7));
  assign out_7 = out_8 ? X : 4'bz;  // Controlled_Buffer controlled_buffer_2
  Pull_Resistor pull_resistor_3 (.node(_2));
  assign _2 = out_10 ? X : 4'bz;  // Controlled_Buffer controlled_buffer_3
  Pull_Resistor pull_resistor_4 (.node(_3));
  assign _3 = out_12 ? X : 4'bz;  // Controlled_Buffer controlled_buffer_4
  Pull_Resistor pull_resistor_5 (.node(_4));
  assign _4 = out_14 ? X : 4'bz;  // Controlled_Buffer controlled_buffer_5
  Pull_Resistor pull_resistor_6 (.node(_5));
  assign _5 = out_16 ? X : 4'bz;  // Controlled_Buffer controlled_buffer_6
  Pull_Resistor pull_resistor_7 (.node(_6));
  assign _6 = out_18 ? X : 4'bz;  // Controlled_Buffer controlled_buffer_7
  Pull_Resistor pull_resistor_8 (.node(_7));
  assign _7 = out_20 ? X : 4'bz;  // Controlled_Buffer controlled_buffer_8

  // Notes on the sheet:
  //   0
  //   1
endmodule

module ALU (
  input  [7:0] in_1,
  input  [7:0] in_2,
  input  in_3,
  input  in_4,
  input  in_5,
  output [7:0] out_6
);

  wire [7:0] adder_8_bit_1_out_4, and_gate_8bit_1_out_3, xor_gate_8bit_1_out_3;

  XOR_Gate_8bit xor_gate_8bit_1 (.in_1(in_1), .in_2(in_2), .out_3(xor_gate_8bit_1_out_3));
  AND_Gate_8bit and_gate_8bit_1 (.in_1(in_1), .in_2(in_2), .out_3(and_gate_8bit_1_out_3));
  ADDER_8_bit adder_8_bit_1 (.A(in_1), .B(in_2), .CIN(1'b0), .out_4(adder_8_bit_1_out_4));  // open: out_5
  assign out_6 = in_4 ? xor_gate_8bit_1_out_3 : 8'bz;  // Controlled_Buffer controlled_buffer_1
  assign out_6 = in_5 ? and_gate_8bit_1_out_3 : 8'bz;  // Controlled_Buffer controlled_buffer_2
  assign out_6 = in_3 ? adder_8_bit_1_out_4 : 8'bz;  // Controlled_Buffer controlled_buffer_3
  Pull_Resistor pull_resistor_1 (.node(out_6));
endmodule

module Right_bitshifter (
  input  [7:0] in_1,
  output [7:0] out_2
);

  Pull_Resistor pull_resistor_1 (.node(out_2[7]));

  assign out_2[6:0] = in_1[7:1];
endmodule

module Left_bitshifter (
  input  [7:0] in_1,
  output [7:0] out_2
);

  Pull_Resistor pull_resistor_1 (.node(out_2[0]));

  assign out_2[7:1] = in_1[6:0];
endmodule

module NOT_Gate (
  input  in_1,
  output out_2
);

  Pull_Resistor pull_resistor_1 (.node(out_2));
  Transistor transistor_1 (.in(1'b1), .out(out_2), .gate(in_1));
endmodule

module NAND_Gate (
  input  in_1,
  input  in_2,
  output out_3
);

  wire transistor_2_out;

  Pull_Resistor #(.pull(1)) pull_resistor_1 (.node(out_3));
  Transistor #(.\type ("n")) transistor_1 (.in(transistor_2_out), .out(out_3), .gate(in_1));
  Transistor #(.\type ("n")) transistor_2 (.in(1'b0), .out(transistor_2_out), .gate(in_2));
endmodule

module AND_Gate_8bit (
  input  [7:0] in_1,
  input  [7:0] in_2,
  output [7:0] out_3
);

  wire nand_gate_1_out_3, nand_gate_2_out_3, nand_gate_3_out_3, nand_gate_4_out_3, nand_gate_5_out_3,
       nand_gate_6_out_3, nand_gate_7_out_3, nand_gate_8_out_3;

  NAND_Gate nand_gate_1 (.in_1(in_1[0]), .in_2(in_2[0]), .out_3(nand_gate_1_out_3));
  NAND_Gate nand_gate_2 (.in_1(in_1[1]), .in_2(in_2[1]), .out_3(nand_gate_2_out_3));
  NAND_Gate nand_gate_3 (.in_1(in_1[2]), .in_2(in_2[2]), .out_3(nand_gate_3_out_3));
  NAND_Gate nand_gate_4 (.in_1(in_1[3]), .in_2(in_2[3]), .out_3(nand_gate_4_out_3));
  NAND_Gate nand_gate_5 (.in_1(in_1[4]), .in_2(in_2[4]), .out_3(nand_gate_5_out_3));
  NAND_Gate nand_gate_6 (.in_1(in_1[5]), .in_2(in_2[5]), .out_3(nand_gate_6_out_3));
  NAND_Gate nand_gate_7 (.in_1(in_1[6]), .in_2(in_2[6]), .out_3(nand_gate_7_out_3));
  NAND_Gate nand_gate_8 (.in_1(in_1[7]), .in_2(in_2[7]), .out_3(nand_gate_8_out_3));
  NOT_Gate not_gate_1 (.in_1(nand_gate_1_out_3), .out_2(out_3[0]));
  NOT_Gate not_gate_2 (.in_1(nand_gate_2_out_3), .out_2(out_3[1]));
  NOT_Gate not_gate_3 (.in_1(nand_gate_3_out_3), .out_2(out_3[2]));
  NOT_Gate not_gate_4 (.in_1(nand_gate_4_out_3), .out_2(out_3[3]));
  NOT_Gate not_gate_5 (.in_1(nand_gate_5_out_3), .out_2(out_3[4]));
  NOT_Gate not_gate_6 (.in_1(nand_gate_6_out_3), .out_2(out_3[5]));
  NOT_Gate not_gate_7 (.in_1(nand_gate_7_out_3), .out_2(out_3[6]));
  NOT_Gate not_gate_8 (.in_1(nand_gate_8_out_3), .out_2(out_3[7]));
endmodule

module NOR_Gate (
  input  in_1,
  input  in_2,
  output out_3
);

  wire transistor_2_out;

  Pull_Resistor pull_resistor_1 (.node(out_3));
  Transistor transistor_1 (.in(transistor_2_out), .out(out_3), .gate(in_1));
  Transistor transistor_2 (.in(1'b1), .out(transistor_2_out), .gate(in_2));
endmodule

module XOR_Gate (
  input  in_1,
  input  in_2,
  output out_3
);

  wire nand_gate_1_out_3, nand_gate_2_out_3, nor_gate_1_out_3, not_gate_1_out_2, not_gate_2_out_2,
       not_gate_3_out_2, not_gate_4_out_2;

  NOT_Gate not_gate_1 (.in_1(in_2), .out_2(not_gate_1_out_2));
  NOT_Gate not_gate_2 (.in_1(in_1), .out_2(not_gate_2_out_2));
  NAND_Gate nand_gate_1 (.in_1(in_1), .in_2(not_gate_1_out_2), .out_3(nand_gate_1_out_3));
  NAND_Gate nand_gate_2 (.in_1(not_gate_2_out_2), .in_2(in_2), .out_3(nand_gate_2_out_3));
  NOT_Gate not_gate_3 (.in_1(nand_gate_1_out_3), .out_2(not_gate_3_out_2));
  NOT_Gate not_gate_4 (.in_1(nand_gate_2_out_3), .out_2(not_gate_4_out_2));
  NOR_Gate nor_gate_1 (.in_1(not_gate_3_out_2), .in_2(not_gate_4_out_2), .out_3(nor_gate_1_out_3));
  NOT_Gate not_gate_5 (.in_1(nor_gate_1_out_3), .out_2(out_3));
endmodule

module XOR_Gate_8bit (
  input  [7:0] in_1,
  input  [7:0] in_2,
  output [7:0] out_3
);

  XOR_Gate xor_gate_1 (.in_1(in_1[0]), .in_2(in_2[0]), .out_3(out_3[0]));
  XOR_Gate xor_gate_2 (.in_1(in_1[1]), .in_2(in_2[1]), .out_3(out_3[1]));
  XOR_Gate xor_gate_3 (.in_1(in_1[2]), .in_2(in_2[2]), .out_3(out_3[2]));
  XOR_Gate xor_gate_4 (.in_1(in_1[3]), .in_2(in_2[3]), .out_3(out_3[3]));
  XOR_Gate xor_gate_5 (.in_1(in_1[4]), .in_2(in_2[4]), .out_3(out_3[4]));
  XOR_Gate xor_gate_6 (.in_1(in_1[5]), .in_2(in_2[5]), .out_3(out_3[5]));
  XOR_Gate xor_gate_7 (.in_1(in_1[6]), .in_2(in_2[6]), .out_3(out_3[6]));
  XOR_Gate xor_gate_8 (.in_1(in_1[7]), .in_2(in_2[7]), .out_3(out_3[7]));
endmodule

module AND_Gate (
  input  in_1,
  input  in_2,
  output out_3
);

  wire nand_gate_1_out_3;

  NAND_Gate nand_gate_1 (.in_1(in_1), .in_2(in_2), .out_3(nand_gate_1_out_3));
  NOT_Gate not_gate_1 (.in_1(nand_gate_1_out_3), .out_2(out_3));
endmodule

module OR_Gate (
  input  in_1,
  input  in_2,
  output out_3
);

  wire nor_gate_1_out_3;

  NOR_Gate nor_gate_1 (.in_1(in_1), .in_2(in_2), .out_3(nor_gate_1_out_3));
  NOT_Gate not_gate_1 (.in_1(nor_gate_1_out_3), .out_2(out_3));
endmodule

module XNOR_Gate (
  input  in_1,
  input  in_2,
  output out_3
);

  wire xor_gate_1_out_3;

  XOR_Gate xor_gate_1 (.in_1(in_1), .in_2(in_2), .out_3(xor_gate_1_out_3));
  NOT_Gate not_gate_1 (.in_1(xor_gate_1_out_3), .out_2(out_3));
endmodule

module AND_Gate_3_input (
  input  in_1,
  input  in_2,
  input  in_3,
  input  in_4,
  input  in_5,
  input  in_6,
  output out_7,
  output out_8
);

  wire not_gate_1_out_2, pull_resistor_1_node, pull_resistor_2_node, pull_resistor_3_node, transistor_2_out,
       transistor_4_out, transistor_6_out, transistor_7_out;

  Pull_Resistor #(.pull(1)) pull_resistor_1 (.node(pull_resistor_1_node));
  Transistor #(.\type ("n")) transistor_1 (.in(transistor_2_out), .out(pull_resistor_1_node), .gate(in_2));
  Transistor #(.\type ("n")) transistor_2 (.in(1'b0), .out(transistor_2_out), .gate(in_3));
  NOT_Gate not_gate_1 (.in_1(pull_resistor_1_node), .out_2(not_gate_1_out_2));
  Pull_Resistor #(.pull(1)) pull_resistor_2 (.node(pull_resistor_2_node));
  Transistor #(.\type ("n")) transistor_3 (.in(transistor_4_out), .out(pull_resistor_2_node), .gate(in_1));
  Transistor #(.\type ("n")) transistor_4 (.in(1'b0), .out(transistor_4_out), .gate(not_gate_1_out_2));
  NOT_Gate not_gate_2 (.in_1(pull_resistor_2_node), .out_2(out_7));
  Pull_Resistor #(.pull(1)) pull_resistor_3 (.node(pull_resistor_3_node));
  Transistor #(.\type ("n")) transistor_5 (.in(transistor_6_out), .out(pull_resistor_3_node), .gate(in_4));
  Transistor #(.\type ("n")) transistor_6 (.in(transistor_7_out), .out(transistor_6_out), .gate(in_5));
  Transistor #(.\type ("n")) transistor_7 (.in(1'b0), .out(transistor_7_out), .gate(in_6));
  NOT_Gate not_gate_3 (.in_1(pull_resistor_3_node), .out_2(out_8));
endmodule

module Multi_input_OR_Gate (
  input  in_1,
  input  in_2,
  input  in_3,
  input  in_4,
  input  in_5,
  input  in_6,
  output out_7,
  output out_8
);

  wire not_gate_1_out_2, pull_resistor_1_node, pull_resistor_2_node, pull_resistor_3_node, transistor_2_out,
       transistor_4_out, transistor_6_out, transistor_7_out;

  Pull_Resistor pull_resistor_1 (.node(pull_resistor_1_node));
  Transistor transistor_1 (.in(transistor_2_out), .out(pull_resistor_1_node), .gate(in_2));
  Transistor transistor_2 (.in(1'b1), .out(transistor_2_out), .gate(in_3));
  NOT_Gate not_gate_1 (.in_1(pull_resistor_1_node), .out_2(not_gate_1_out_2));
  Pull_Resistor pull_resistor_2 (.node(pull_resistor_2_node));
  Transistor transistor_3 (.in(transistor_4_out), .out(pull_resistor_2_node), .gate(in_1));
  Transistor transistor_4 (.in(1'b1), .out(transistor_4_out), .gate(not_gate_1_out_2));
  NOT_Gate not_gate_2 (.in_1(pull_resistor_2_node), .out_2(out_7));
  Pull_Resistor pull_resistor_3 (.node(pull_resistor_3_node));
  Transistor transistor_5 (.in(transistor_6_out), .out(pull_resistor_3_node), .gate(in_4));
  Transistor transistor_6 (.in(transistor_7_out), .out(transistor_6_out), .gate(in_5));
  Transistor transistor_7 (.in(1'b1), .out(transistor_7_out), .gate(in_6));
  NOT_Gate not_gate_3 (.in_1(pull_resistor_3_node), .out_2(out_8));
endmodule

module Half_adder (
  input  in_1,
  input  in_2,
  output out_3
);

  XOR_Gate xor_gate_1 (.in_1(in_1), .in_2(in_2), .out_3(out_3));
endmodule

module ODD (
  input  in_1,
  input  in_2,
  input  CIN,
  output out_4
);

  wire and_gate_1_out_3, and_gate_2_out_3, not_gate_1_out_2, not_gate_2_out_2, xor_gate_1_out_3;

  XOR_Gate xor_gate_1 (.in_1(in_1), .in_2(in_2), .out_3(xor_gate_1_out_3));
  NOT_Gate not_gate_1 (.in_1(xor_gate_1_out_3), .out_2(not_gate_1_out_2));
  NOT_Gate not_gate_2 (.in_1(CIN), .out_2(not_gate_2_out_2));
  AND_Gate and_gate_1 (.in_1(not_gate_1_out_2), .in_2(CIN), .out_3(and_gate_1_out_3));
  AND_Gate and_gate_2 (.in_1(not_gate_2_out_2), .in_2(xor_gate_1_out_3), .out_3(and_gate_2_out_3));
  OR_Gate or_gate_1 (.in_1(and_gate_2_out_3), .in_2(and_gate_1_out_3), .out_3(out_4));
endmodule

module MAJ (
  input  in_1,
  input  in_2,
  input  CIN,
  output out_4
);

  wire and_gate_1_out_3, and_gate_2_out_3, or_gate_1_out_3;

  OR_Gate or_gate_1 (.in_1(in_1), .in_2(in_2), .out_3(or_gate_1_out_3));
  AND_Gate and_gate_1 (.in_1(in_1), .in_2(in_2), .out_3(and_gate_1_out_3));
  AND_Gate and_gate_2 (.in_1(or_gate_1_out_3), .in_2(CIN), .out_3(and_gate_2_out_3));
  OR_Gate or_gate_2 (.in_1(and_gate_2_out_3), .in_2(and_gate_1_out_3), .out_3(out_4));
endmodule

module Full_Adder_1bit (
  input  A,
  input  B,
  input  CIN,
  output SUM,
  output COUT
);

  MAJ maj_1 (.in_1(A), .in_2(B), .CIN(CIN), .out_4(COUT));
  ODD odd_1 (.in_1(A), .in_2(B), .CIN(CIN), .out_4(SUM));
  // Probe on {COUT, SUM}
endmodule

module Ripple_Carry_Adder_8bit (
  input  [7:0] A,
  input  [7:0] B,
  input  CIN,
  output [7:0] out_4,
  output out_5
);

  wire full_adder_1bit_1_cout, full_adder_1bit_2_cout, full_adder_1bit_3_cout, full_adder_1bit_4_cout,
       full_adder_1bit_5_cout, full_adder_1bit_6_cout, full_adder_1bit_7_cout;

  // Probe on B
  // Probe on A
  Full_Adder_1bit full_adder_1bit_1 (.A(A[0]), .B(B[0]), .CIN(CIN), .SUM(out_4[0]), .COUT(full_adder_1bit_1_cout));
  Full_Adder_1bit full_adder_1bit_2 (
    .A(A[1]), .B(B[1]), .CIN(full_adder_1bit_1_cout), .SUM(out_4[1]), .COUT(full_adder_1bit_2_cout));
  Full_Adder_1bit full_adder_1bit_3 (
    .A(A[2]), .B(B[2]), .CIN(full_adder_1bit_2_cout), .SUM(out_4[2]), .COUT(full_adder_1bit_3_cout));
  Full_Adder_1bit full_adder_1bit_4 (
    .A(A[3]), .B(B[3]), .CIN(full_adder_1bit_3_cout), .SUM(out_4[3]), .COUT(full_adder_1bit_4_cout));
  Full_Adder_1bit full_adder_1bit_5 (
    .A(A[4]), .B(B[4]), .CIN(full_adder_1bit_4_cout), .SUM(out_4[4]), .COUT(full_adder_1bit_5_cout));
  Full_Adder_1bit full_adder_1bit_6 (
    .A(A[5]), .B(B[5]), .CIN(full_adder_1bit_5_cout), .SUM(out_4[5]), .COUT(full_adder_1bit_6_cout));
  Full_Adder_1bit full_adder_1bit_7 (
    .A(A[6]), .B(B[6]), .CIN(full_adder_1bit_6_cout), .SUM(out_4[6]), .COUT(full_adder_1bit_7_cout));
  Full_Adder_1bit full_adder_1bit_8 (.A(A[7]), .B(B[7]), .CIN(full_adder_1bit_7_cout), .SUM(out_4[7]), .COUT(out_5));
  // Probe on {out_5, out_4}
endmodule

module ALU_8bit (
  input  [7:0] A,
  input  [7:0] B,
  input  S2,
  input  S1,
  input  S0,
  output [7:0] O
);

  wire de_coder_1__1, de_coder_1__2, de_coder_1__3, de_coder_1__4, de_coder_1__5, de_coder_1__6;
  wire [7:0] and_gate_8bit_1_out_3, left_bitshifter_1_out_2, right_bitshifter_1_out_2,
       ripple_carry_adder_8bit_1_out_4, substractor_8_bit_1_out_4, xor_gate_8bit_1_out_3;

  // Probe on A
  // Probe on B
  Ripple_Carry_Adder_8bit ripple_carry_adder_8bit_1 (
    .A(A), .B(B), .CIN(1'b0), .out_4(ripple_carry_adder_8bit_1_out_4));  // open: out_5
  XOR_Gate_8bit xor_gate_8bit_1 (.in_1(A), .in_2(B), .out_3(xor_gate_8bit_1_out_3));
  AND_Gate_8bit and_gate_8bit_1 (.in_1(A), .in_2(B), .out_3(and_gate_8bit_1_out_3));
  Substractor_8_bit substractor_8_bit_1 (.A(A), .B(B), .CIN(1'b0), .out_4(substractor_8_bit_1_out_4));  // open: out_5
  Right_bitshifter right_bitshifter_1 (.in_1(A), .out_2(right_bitshifter_1_out_2));
  Left_bitshifter left_bitshifter_1 (.in_1(A), .out_2(left_bitshifter_1_out_2));
  De_Coder de_coder_1 (
    .in_1(S2), .in_2(S1), .in_3(S0), ._1(de_coder_1__1), ._2(de_coder_1__2), ._3(de_coder_1__3),
    ._4(de_coder_1__4), ._5(de_coder_1__5), ._6(de_coder_1__6));  // open: _0, _7
  one_hot_mux_8bit one_hot_mux_8bit_1 (
    .ADD(ripple_carry_adder_8bit_1_out_4), .X(xor_gate_8bit_1_out_3), .AN(and_gate_8bit_1_out_3),
    .SUB(substractor_8_bit_1_out_4), .RS(right_bitshifter_1_out_2), .LS(left_bitshifter_1_out_2),
    .CADD(de_coder_1__1), .CX(de_coder_1__2), .CAN(de_coder_1__3), .CSUB(de_coder_1__4), .CRS(de_coder_1__5),
    .CLS(de_coder_1__6), .O(O));
  // Probe on O
endmodule

module one_hot_mux_1bit (
  input  A,
  input  B,
  input  C,
  input  C1,
  input  C2,
  input  C3,
  output O
);

  wire and_gate_1_out_3, and_gate_2_out_3, and_gate_3_out_3;

  AND_Gate and_gate_1 (.in_1(A), .in_2(C1), .out_3(and_gate_1_out_3));
  AND_Gate and_gate_2 (.in_1(B), .in_2(C2), .out_3(and_gate_2_out_3));
  AND_Gate and_gate_3 (.in_1(C), .in_2(C3), .out_3(and_gate_3_out_3));
  or or_1 (O, and_gate_1_out_3, and_gate_2_out_3, and_gate_3_out_3);
endmodule

module one_hot_mux_8bit (
  input  [7:0] ADD,
  input  [7:0] X,
  input  [7:0] AN,
  input  [7:0] SUB,
  input  [7:0] RS,
  input  [7:0] LS,
  input  CADD,
  input  CX,
  input  CAN,
  input  CSUB,
  input  CRS,
  input  CLS,
  output [7:0] O
);

  wire [7:0] and_gate_8bit_1_out_3, and_gate_8bit_2_out_3, and_gate_8bit_3_out_3, and_gate_8bit_4_out_3,
       and_gate_8bit_5_out_3, and_gate_8bit_6_out_3, or_1_out, or_2_out;

  AND_Gate_8bit and_gate_8bit_1 (.in_1(ADD), .in_2({8{CADD}}), .out_3(and_gate_8bit_1_out_3));
  AND_Gate_8bit and_gate_8bit_2 (.in_1(X), .in_2({8{CX}}), .out_3(and_gate_8bit_2_out_3));
  AND_Gate_8bit and_gate_8bit_3 (.in_1(AN), .in_2({8{CAN}}), .out_3(and_gate_8bit_3_out_3));
  AND_Gate_8bit and_gate_8bit_4 (.in_1(SUB), .in_2({8{CSUB}}), .out_3(and_gate_8bit_4_out_3));
  AND_Gate_8bit and_gate_8bit_5 (.in_1(RS), .in_2({8{CRS}}), .out_3(and_gate_8bit_5_out_3));
  AND_Gate_8bit and_gate_8bit_6 (.in_1(LS), .in_2({8{CLS}}), .out_3(and_gate_8bit_6_out_3));
  assign or_1_out = and_gate_8bit_1_out_3 | and_gate_8bit_2_out_3 | and_gate_8bit_3_out_3;  // OR_Gate_part or_1, 8 bits wide
  assign or_2_out = and_gate_8bit_4_out_3 | and_gate_8bit_5_out_3 | and_gate_8bit_6_out_3;  // OR_Gate_part or_2, 8 bits wide
  assign O = or_1_out | or_2_out;  // OR_Gate_part or_3, 8 bits wide
endmodule

module Full_Substractor (
  input  A,
  input  B,
  input  CIN,
  output SUM,
  output COUT
);

  wire and_1_out, and_2_out, not_1_out, not_2_out, xor_1_out;

  not not_1 (not_1_out, A);
  xor xor_1 (xor_1_out, A, B);
  not not_2 (not_2_out, xor_1_out);
  and and_1 (and_1_out, not_1_out, B);
  xor xor_2 (SUM, xor_1_out, CIN);
  and and_2 (and_2_out, not_2_out, CIN);
  or or_1 (COUT, and_1_out, and_2_out);
  // Probe on {COUT, SUM}
endmodule

module Substractor_8_bit (
  input  [7:0] A,
  input  [7:0] B,
  input  CIN,
  output [7:0] out_4,
  output out_5
);

  wire full_substractor_1_cout, full_substractor_2_cout, full_substractor_3_cout, full_substractor_4_cout,
       full_substractor_5_cout, full_substractor_6_cout, full_substractor_7_cout;

  // Probe on B
  // Probe on A
  Full_Substractor full_substractor_1 (.A(A[0]), .B(B[0]), .CIN(CIN), .SUM(out_4[0]), .COUT(full_substractor_1_cout));
  Full_Substractor full_substractor_2 (
    .A(A[1]), .B(B[1]), .CIN(full_substractor_1_cout), .SUM(out_4[1]), .COUT(full_substractor_2_cout));
  Full_Substractor full_substractor_3 (
    .A(A[2]), .B(B[2]), .CIN(full_substractor_2_cout), .SUM(out_4[2]), .COUT(full_substractor_3_cout));
  Full_Substractor full_substractor_4 (
    .A(A[3]), .B(B[3]), .CIN(full_substractor_3_cout), .SUM(out_4[3]), .COUT(full_substractor_4_cout));
  Full_Substractor full_substractor_5 (
    .A(A[4]), .B(B[4]), .CIN(full_substractor_4_cout), .SUM(out_4[4]), .COUT(full_substractor_5_cout));
  Full_Substractor full_substractor_6 (
    .A(A[5]), .B(B[5]), .CIN(full_substractor_5_cout), .SUM(out_4[5]), .COUT(full_substractor_6_cout));
  Full_Substractor full_substractor_7 (
    .A(A[6]), .B(B[6]), .CIN(full_substractor_6_cout), .SUM(out_4[6]), .COUT(full_substractor_7_cout));
  Full_Substractor full_substractor_8 (.A(A[7]), .B(B[7]), .CIN(full_substractor_7_cout), .SUM(out_4[7]), .COUT(out_5));
  // Probe on {out_5, out_4}
  // Probe on out_4
endmodule

module ALU_8bit_WOD (
  input  [7:0] A,
  input  [7:0] B,
  input  CADD,
  input  CX,
  input  CAN,
  input  CSUB,
  input  CRS,
  input  CLS,
  output [7:0] O
);

  wire [7:0] and_gate_8bit_1_out_3, left_bitshifter_1_out_2, right_bitshifter_1_out_2,
       ripple_carry_adder_8bit_1_out_4, substractor_8_bit_1_out_4, xor_gate_8bit_1_out_3;

  // Probe on A
  // Probe on B
  Ripple_Carry_Adder_8bit ripple_carry_adder_8bit_1 (
    .A(A), .B(B), .CIN(1'b0), .out_4(ripple_carry_adder_8bit_1_out_4));  // open: out_5
  XOR_Gate_8bit xor_gate_8bit_1 (.in_1(A), .in_2(B), .out_3(xor_gate_8bit_1_out_3));
  AND_Gate_8bit and_gate_8bit_1 (.in_1(A), .in_2(B), .out_3(and_gate_8bit_1_out_3));
  Substractor_8_bit substractor_8_bit_1 (.A(A), .B(B), .CIN(1'b0), .out_4(substractor_8_bit_1_out_4));  // open: out_5
  Right_bitshifter right_bitshifter_1 (.in_1(A), .out_2(right_bitshifter_1_out_2));
  Left_bitshifter left_bitshifter_1 (.in_1(A), .out_2(left_bitshifter_1_out_2));
  one_hot_mux_8bit one_hot_mux_8bit_1 (
    .ADD(ripple_carry_adder_8bit_1_out_4), .X(xor_gate_8bit_1_out_3), .AN(and_gate_8bit_1_out_3),
    .SUB(substractor_8_bit_1_out_4), .RS(right_bitshifter_1_out_2), .LS(left_bitshifter_1_out_2),
    .CADD(CADD), .CX(CX), .CAN(CAN), .CSUB(CSUB), .CRS(CRS), .CLS(CLS), .O(O));
  // Probe on O
endmodule
